# Fritzing sketch project (saved by Fritzing 0.9.3b)
breadboards: 2

parts:
  R1 = Resistor [tolerance=±5% resistance=100 package=THT]
  R2 = Resistor [tolerance=±5% resistance=100 package=THT]
  R3 = Resistor [tolerance=±5% resistance=100 package=THT]
  R4 = Resistor [tolerance=±5% resistance=100 package=THT]
  R5 = Resistor [tolerance=±5% resistance=100 package=THT]
  R6 = Resistor [tolerance=±5% resistance=100 package=THT]
  R7 = Resistor [tolerance=±5% resistance=100 package=THT]
  R8 = Resistor [tolerance=±5% resistance=100 package=THT]
  R9 = Resistor [tolerance=±5% resistance=100 package=THT]
  R10 = Resistor [tolerance=±5% resistance=100 package=THT]
  R11 = Resistor [tolerance=±5% resistance=100 package=THT]
  R12 = Resistor [tolerance=±5% resistance=100 package=THT]
  R13 = Resistor [tolerance=±5% resistance=100 package=THT]
  R14 = Resistor [tolerance=±5% resistance=100 package=THT]
  R15 = Resistor [tolerance=±5% resistance=100 package=THT]
  R16 = Resistor [tolerance=±5% resistance=100 package=THT]
  IC1 = DIP - 20 pins [chip_label=74LS573 package="DIP (Dual Inline) [THT]"]
  IC2 = DIP - 20 pins [chip_label=74LS573 package="DIP (Dual Inline) [THT]"]
  Disp1 = LBT2088AH [part_number=LBT2088AH]
  Part1 = Arduino Uno (Rev3)
  R17 = Resistor [tolerance=±5% resistance=1k package=THT]
  R18 = Resistor [tolerance=±5% resistance=1k package=THT]
  R19 = Resistor [tolerance=±5% resistance=1k package=THT]
  R20 = Resistor [tolerance=±5% resistance=1k package=THT]
  R21 = Resistor [tolerance=±5% resistance=1k package=THT]
  R22 = Resistor [tolerance=±5% resistance=1k package=THT]
  R24 = Resistor [tolerance=±5% resistance=1k package=THT]
  R25 = Resistor [tolerance=±5% resistance=1k package=THT]
  R26 = Resistor [tolerance=±5% resistance=1k package=THT]
  R23 = Resistor [tolerance=±5% resistance=1k package=THT]

nets:
  N1: R1.Pin_0, IC1.O7
  N2: R1.Pin_1, Disp1.pin_16
  N3: R2.Pin_0, IC1.O6
  N4: R2.Pin_1, Disp1.pin_15
  N5: R3.Pin_0, IC1.O5
  N6: R3.Pin_1, Disp1.pin_11
  N7: R4.Pin_0, IC1.O4
  N8: R4.Pin_1, Disp1.pin_6
  N9: R5.Pin_0, IC1.O3
  N10: R5.Pin_1, Disp1.pin_10
  N11: R6.Pin_0, IC1.O2
  N12: R6.Pin_1, Disp1.pin_4
  N13: R7.Pin_0, IC1.O1
  N14: R7.Pin_1, Disp1.pin_3
  N15: R8.Pin_0, IC1.O0
  N16: R8.Pin_1, Disp1.pin_13
  N17: R9.Pin_0, Disp1.pin_9
  N18: R9.Pin_1, IC2.O0
  N19: R10.Pin_0, Disp1.pin_14
  N20: R10.Pin_1, IC2.O1
  N21: R11.Pin_0, Disp1.pin_8
  N22: R11.Pin_1, IC2.O2
  N23: R12.Pin_0, Disp1.pin_12
  N24: R12.Pin_1, IC2.O3
  N25: R13.Pin_0, Disp1.pin1
  N26: R13.Pin_1, IC2.O4
  N27: R14.Pin_0, Disp1.pin_7
  N28: R14.Pin_1, IC2.O5
  N29: R15.Pin_0, Disp1.pin2
  N30: R15.Pin_1, IC2.O6
  N31: R16.Pin_0, Disp1.pin_5
  N32: R16.Pin_1, IC2.O7
  GND: IC1.OE, IC2.GND, Part1.GND
  N33: IC1.D0, IC2.D0, Part1.D4, R24.Pin_1
  N34: IC1.D1, IC2.D1, Part1.D5_PWM, R23.Pin_1
  N35: IC1.D3#3, IC2.D3#3, Part1.D6_PWM, R22.Pin_1
  N36: IC1.D3#4, IC2.D3#4, Part1.D7, R21.Pin_1
  N37: IC1.D4, IC2.D4, Part1.D8, R20.Pin_1
  N38: IC1.D5, IC2.D5, Part1.D9_PWM, R19.Pin_1
  N39: IC1.D6, IC2.D6, Part1.D10_PWM/SS, R18.Pin_1
  N40: IC1.D7, IC2.D7, Part1.D11_PWM/MOSI, R17.Pin_1
  N41: IC1.GND, IC2.OE
  N42: IC1.LE, R25.Pin_1
  VCC: IC1.Vcc, IC2.Vcc, Part1.5V, R17.Pin_0, R18.Pin_0, R19.Pin_0, R20.Pin_0, R21.Pin_0, R22.Pin_0, R24.Pin_0, R23.Pin_0
  N43: IC2.LE, R26.Pin_1
  N44: Part1.D2, R26.Pin_0
  N45: Part1.D3_PWM, R25.Pin_0

custom parts:
  DIP - 20 pins: A DIP stand-in part for whatever IC you want. With 20 pins on a 300mil dual inline package (DIP) footprint.
